# Fritzing sketch Sketch (saved by Fritzing 0.9.9b)
circuit board: 8.46667cm x 5.64444cm

parts:
  Pololu_A1 = Pololu A4988 [package=SO16]
  Pololu_A2 = Pololu A4988 [package=SO16]
  Esp32-cam1 = ESP32-Cam
  M1 = DOIT Esp32 DevKit v1 (30 pins long, 11 pins width) [part_number=ESP32S-PIN30]
  Raspberry_Pi_1 = Raspberry Pi 3 [part_number=RPI-3-V1.2]
  M2 = Stepper Motor - Bipolar
  M3 = Stepper Motor - Bipolar
  Power_plug1 = Power plug
  Power_plug2 = Power plug  # not connected
  S7 = Limit Switch [package="Breakout Board"]
  S8 = Limit Switch [package="Breakout Board"]

nets:
  N1: Pololu_A1.RESET, Pololu_A1.SLEEP
  N2: Pololu_A1.STEP, M1.D26
  N3: Pololu_A1.DIR, M1.D27
  GND: Pololu_A1.GND#8, Pololu_A2.GND#8, Esp32-cam1.GND, M1.GND, Raspberry_Pi_1.GND, Power_plug1.GND
  VDD: Pololu_A1.VDD, Pololu_A2.VDD, Esp32-cam1.5V, M1.VIN, Raspberry_Pi_1.5V, Power_plug1.VCC
  N4: Pololu_A1.1B, M2.D
  N5: Pololu_A1.1A, M2.B
  N6: Pololu_A1.2A, M2.C
  N7: Pololu_A1.2B, M2.A
  N8: Pololu_A1.GND#14, Pololu_A2.GND#14
  N9: Pololu_A1.VMOT, Pololu_A2.VMOT
  N10: Pololu_A2.RESET, Pololu_A2.SLEEP
  N11: Pololu_A2.STEP, M1.D12
  N12: Pololu_A2.DIR, M1.D14
  N13: Pololu_A2.1B, M3.D
  N14: Pololu_A2.1A, M3.B
  N15: Pololu_A2.2A, M3.C
  N16: Pololu_A2.2B, M3.A
  N17: M1.3V3, S7.S, S8.S
  N18: M1.D15, S7.V
  N19: M1.D2, S8.V

notes:
  24v (motor)
  5v (logic)
  Raspberry Pi - Controller
  Drawer Stepper
  Camera Stepper
  ESP32
  ESP32-CAM
  Limit
  Switches
  A4988

custom parts:
  DOIT Esp32 DevKit v1 (30 pins long, 11 pins width): The DOIT Esp32 DevKit v1 is one of the development board created by DOIT to evaluate the ESP-WROOM-32 module. It is based on the ESP32 microcontroller that boasts Wifi, Bluetooth, Ethernet and Low Power support all in a single chip. (vanepp) made breadboard work, adjusted pin numbering and labels and reduced size of schematic and cleaned up pcb. This chip is 30pins long (2 x15) and 11 pins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
  Limit Switch: Generic limit switch commonly found on 3D printers. Typical lever microswitch mounted on a PCB board with a 3 pin JST XH connector.
